# Fritzing sketch alarm (saved by Fritzing 0.9.2b)
circuit board: 8.46667cm x 5.64444cm
breadboards: 1

parts:
  Part1 = Arduino Uno (Rev3)
  LED1 = LED - 5mm [color="Red (633nm)" package="5 mm [THT]"]
  Reed_Switch = Reed switch [package=THT]

nets:
  N1: Part1.D13/SCK, LED1.anode
  N2: Part1.GND, LED1.cathode
  N3: Part1.D7, Reed_Switch.pin_1
  N4: Part1.3V3, Reed_Switch.pin_2
